// Logisim project CircuitQ15.circ as structural Verilog: 1 circuit, main circuit main
module main (
  input  A,
  input  B,
  input  C,
  input  D,
  output Output
);

  wire and_1_out, or_1_out;

  and and_1 (and_1_out, A, B);
  or or_1 (or_1_out, and_1_out, C);
  and and_2 (Output, or_1_out, D);

  // Notes on the sheet:
  //   (AB)
  //   (AB + C)
  //   (AB + C) D
endmodule
